# Fritzing sketch IBT-2 speed controller (saved by Fritzing 0.9.9b)

parts:
  IBT_2 = IBT-2_bridge
  Part2 = Arduino Prototyping Shield
  Switch_with_LED = Waterproof Pushbutton (red)
  Speed_Control = Rotary Potentiometer (Small) [maximum_resistance=100kΩ package=THT]
  Resistor = Resistor [tolerance=±5% power=0.25 resistance=470 package=THT]
  Compressor = DC Motor
  12VDC_PSU1 = 12VDC Power Supply generic [part_number="12VDC PSU"]
  Set_to_5VDC_out = Generic DC DC converter [part_number="DC DC converter"]

nets:
  N1: IBT_2.connector42, IBT_2.connector43, Part2.D5
  N2: IBT_2.connector44, IBT_2.connector45, Part2.D4, Part2.N$431, Resistor.Pin_0
  N3: IBT_2.connector48, Part2.+5V, Speed_Control.leg2, Set_to_5VDC_out.DC_Out+
  N4: IBT_2.connector49, Part2.GND, Switch_with_LED.no_name_yet#1, Switch_with_LED.no_name_yet#5, Speed_Control.leg1, Set_to_5VDC_out.DC_Out-
  N5: IBT_2.connector50, 12VDC_PSU1.DC-, Set_to_5VDC_out.DC_In-
  N6: IBT_2.connector51, 12VDC_PSU1.DC+, Set_to_5VDC_out.DC_In+
  N7: IBT_2.connector52, Compressor.pin_1
  N8: IBT_2.connector53, Compressor.pin_2
  N9: Part2.D8, Part2.N$77, Switch_with_LED.no_name_yet#2
  N10: Part2.A0, Part2.N$72, Speed_Control.wiper
  N11: Part2.N$86, Part2.N$378, Switch_with_LED.no_name_yet#4, Resistor.Pin_1

custom parts:
  Waterproof Pushbutton (red): Waterproof Illuminated Pushbutton (red)
  12VDC Power Supply generic: AC-DC 100V-220V to 12V Power Supply Module
  Generic DC DC converter: DC DC converter module
